# Fritzing sketch XBeeWiring (saved by Fritzing 0.9.6b)

parts:
  Raspberry_Pi_B_rev1 = Raspberry Pi B rev1
  U2 = XBee
  LED1 = LED - 3mm [color="Green (565nm)" current=0.030 package="3 mm [THT]"]
  LED2 = LED - 3mm [color="Red (633nm)" current=0.030 package="3 mm [THT]"]
  R1 = Resistor [tolerance=±5% power=0.25 resistance=1000 package=THT]
  Q1 = NPN-Transistor [package="TO92 [THT]"]
  R2 = Resistor [tolerance=±5% power=0.25 resistance=1000 package=THT]
  R3 = Resistor [tolerance=±5% power=0.25 resistance=10000 package=THT]

nets:
  3V3: Raspberry_Pi_B_rev1.3V3, U2.VCC
  N1: Raspberry_Pi_B_rev1.5V, Q1.C
  GND: Raspberry_Pi_B_rev1.GND, U2.GND, R1.Pin_0, R2.Pin_0, R3.Pin_0
  N2: Raspberry_Pi_B_rev1.GPIO_14, U2.pin3
  N3: Raspberry_Pi_B_rev1.GPIO_15, U2.pin2
  N4: Raspberry_Pi_B_rev1.GPIO_21, Q1.B
  N5: U2.pin5, R1.Pin_1, Q1.E
  N6: U2.pin6, LED2.anode
  N7: U2.pin15, LED1.anode
  N8: LED1.cathode, R3.Pin_1
  N9: LED2.cathode, R2.Pin_1
